// Logisim project HappySwitch.circ as structural Verilog: 1 circuit, main circuit main
module main (
  input  in_1
);

  wire [3:0] multiplexer_1_out, multiplexer_2_out;

  Multiplexer #(.width(4), .disabled(0)) multiplexer_1 (
    .in0(4'b1111), .in1(4'b1001), .out(multiplexer_1_out), .sel(in_1), .en(1'b1));
  Multiplexer #(.width(4), .disabled(0)) multiplexer_2 (
    .in0(4'b1001), .in1(4'b1111), .out(multiplexer_2_out), .sel(in_1), .en(1'b1));
  DotMatrix #(.inputtype("row"), .matrixcols(4), .matrixrows(4)) dotmatrix_1 (
    .row0(4'b1001), .row1(4'b0000), .row2(multiplexer_1_out), .row3(multiplexer_2_out));
endmodule
